# Fritzing sketch alimenta_led (saved by Fritzing 0.9.3b)
breadboards: 1

parts:
  R1 = Resistor [tolerance=±5% resistance=680 package=THT]
  Componente1 = Arduino Uno (Rev3)
  LED1 = LED - 5mm [color="Red (633nm)" package="5 mm [THT]"]

nets:
  N1: R1.Pin_0, Componente1.5V
  N2: R1.Pin_1, LED1.cathode
  N3: Componente1.GND, LED1.anode
