# Fritzing sketch botao_e_buzzer (saved by Fritzing 0.9.3b)
breadboards: 1

parts:
  Componente1 = Arduino Uno (Rev3)
  S1 = Pushbutton [package="[THT]"]
  R2 = Resistor [tolerance=±5% resistance=330k package=THT]
  J1 = Piezo Speaker

nets:
  N1: Componente1.D3_PWM, J1.pin2
  N2: Componente1.D4, S1.Pin_3, S1.Pin_4, R2.Pin_1
  N3: Componente1.5V, R2.Pin_0
  N4: Componente1.GND, S1.Pin_1, S1.Pin_2, J1.pin1

// code stored in the sketch: liga_led_arduino.ino

const int buttonPin = 4;
const int ledPin       = 3;
int ledValue;

void setup(){
	pinMode(ledPin,OUTPUT);
	pinMode(buttonPin,INPUT);
}

void loop(){
	ledValue = digitalRead(buttonPin);
	digitalWrite(ledPin,ledValue);
}
