# Fritzing sketch comunicação RF v2 (saved by Fritzing 0.9.3b)
breadboards: 1

parts:
  S1 = Pushbutton [package="[THT]"]
  S2 = Pushbutton [package="[THT]"]
  Componente1 = NRF24L01+ Breakout Board
  Componente2 = Arduino Uno (Rev3)
  R1 = Resistor [tolerance=±5% resistance=10k package=THT]
  R2 = Resistor [tolerance=±5% resistance=10k package=THT]
  LED1 = RGB LED (com. cathode, rgb) [package="5 mm [THT]"]
  R3 = Resistor [tolerance=±5% resistance=220 package=THT]
  R4 = Resistor [tolerance=±5% resistance=220 package=THT]
  R5 = Resistor [tolerance=±5% resistance=220 package=THT]

nets:
  N1: S1.Pin_1, S1.Pin_2, Componente2.A0, R2.Pin_1
  VCC: S1.Pin_3, S1.Pin_4, S2.Pin_3, S2.Pin_4, Componente1.VCC, Componente2.5V
  N2: S2.Pin_1, S2.Pin_2, Componente2.A1, R1.Pin_1
  GND: Componente1.GND, Componente2.GND, R1.Pin_0, R2.Pin_0
  N3: Componente1.CE, Componente2.D8
  N4: Componente1.CS, Componente2.D7
  N5: Componente1.SCK, Componente2.D13/SCK
  N6: Componente1.MOSI, Componente2.D11_PWM/MOSI
  N7: Componente1.MISO, Componente2.D12/MISO
  N8: Componente2.A2, R3.Pin_0
  N9: Componente2.A3, R4.Pin_1
  N10: Componente2.A4/SDA, R5.Pin_1
  N11: LED1.red_anode, R3.Pin_1
  N12: LED1.green_anode, R4.Pin_0
  N13: LED1.blue_anode, R5.Pin_0
