# Fritzing sketch lcd (saved by Fritzing 0.9.3b)
breadboards: 1

parts:
  R14 = Rotary Potentiometer (Large) [maximum_resistance=10kΩ package=THT]
  LCD1 = LCD screen
  Arduino2 = Arduino Uno (Rev3)

nets:
  N1: R14.wiper, LCD1.DB7, Arduino2.D2
  VSS: LCD1.VSS, LCD1.R/W, Arduino2.GND
  VDD: LCD1.VDD, Arduino2.5V
  N2: LCD1.RS, Arduino2.D12/MISO
  N3: LCD1.E, Arduino2.D11_PWM/MOSI
  N4: LCD1.DB4, Arduino2.D5_PWM
  N5: LCD1.DB5, Arduino2.D4
  N6: LCD1.DB6, Arduino2.D3_PWM

// code stored in the sketch: big_smiley.ino
#include <LiquidCrystal.h>

LiquidCrystal lcd(12, 11, 5, 4, 3, 2);

byte smiley00[8] = {
  B00000,
  B00000,
  B00011,
  B00100,
  B01000,
  B01000,
  B10000,
  B10000
};
byte smiley10[8] = {
  B00000,
  B11111,
  B00000,
  B00000,
  B00000,
  B10001,
  B10001,
  B00000
};
byte smiley20[8] = {
  B00000,
  B00000,
  B11000,
  B00100,
  B00010,
  B00010,
  B00001,
  B00001
};
byte smiley01[8] = {
  B10000,
  B10001,
  B10000,
  B01000,
  B01000,
  B00100,
  B00011,
  B00000
};
byte smiley11[8] = {
  B00000,
  B00000,
  B10001,
  B01110,
  B00000,
  B00000,
  B00000,
  B11111
};
byte smiley21[8] = {
  B00001,
  B10001,
  B00001,
  B00010,
  B00010,
  B00100,
  B11000,
  B00000
};

void setup() {
  lcd.createChar(0, smiley00);
  lcd.createChar(1, smiley10);
  lcd.createChar(2, smiley20);
  lcd.createChar(4, smiley01);
  lcd.createChar(5, smiley11);
  lcd.createChar(6, smiley21);
  lcd.begin(16, 2);  
  lcd.write(byte(0));
  lcd.write(byte(1));
  lcd.write(byte(2));
  lcd.setCursor(0, 1);
  lcd.write(byte(4));
  lcd.write(byte(5));
  lcd.write(byte(6));
  delay(1000);
  lcd.createChar(6, smiley20);
}

void loop() {}

// code stored in the sketch: ciencia_6.ino
/*
  LiquidCrystal Library - Hello World
 
 Demonstrates the use a 16x2 LCD display.  The LiquidCrystal
 library works with all LCD displays that are compatible with the 
 Hitachi HD44780 driver. There are many of them out there, and you
 can usually tell them by the 16-pin interface.
 
 This sketch prints "Hello World!" to the LCD
 and shows the time.
 
  The circuit:
 * LCD RS pin to digital pin 12
 * LCD Enable pin to digital pin 11
 * LCD D4 pin to digital pin 5
 * LCD D5 pin to digital pin 4
 * LCD D6 pin to digital pin 3
 * LCD D7 pin to digital pin 2
 * LCD R/W pin to ground
 * 10K resistor:
 * ends to +5V and ground
 * wiper to LCD VO pin (pin 3)
 
 Library originally added 18 Apr 2008
 by David A. Mellis
 library modified 5 Jul 2009
 by Limor Fried (http://www.ladyada.net)
 example added 9 Jul 2009
 by Tom Igoe
 modified 22 Nov 2010
 by Tom Igoe
 
 This example code is in the public domain.

 http://www.arduino.cc/en/Tutorial/LiquidCrystal
 */

// include the library code:
#include <LiquidCrystal.h>

// initialize the library with the numbers of the interface pins
LiquidCrystal lcd(12, 11, 5, 4, 3, 2);

const int echoPin = 7;
const int trigPin = 6;

void setup() {
  pinMode(echoPin,INPUT);
  pinMode(trigPin,OUTPUT);
  // set up the LCD's number of columns and rows: 
  lcd.begin(16, 2);
  // Print a message to the LCD.
  lcd.print("hello, world!");
  Serial.begin(9600);
}

void loop() {
  //seta o pino 12 com um pulso baixo "LOW" ou desligado ou ainda 0  
    digitalWrite(trigPin, LOW);  
  // delay de 2 microssegundos  
    delayMicroseconds(2);  
  //seta o pino 12 com pulso alto "HIGH" ou ligado ou ainda 1  
    digitalWrite(trigPin, HIGH);  
  //delay de 10 microssegundos  
    delayMicroseconds(10);  
  //seta o pino 12 com pulso baixo novamente  
    digitalWrite(trigPin, LOW);  
  //pulseInt lê o tempo entre a chamada e o pino entrar em high  
    long duration = pulseIn(echoPin,HIGH);  
  //Esse calculo é baseado em s = v . t, lembrando que o tempo vem dobrado  
  //porque é o tempo de ida e volta do ultrassom  
    long distancia = duration /29 / 2 ;  
   // set the cursor to column 0, line 1
  // (note: line 1 is the second row, since counting begins with 0):
  lcd.setCursor(0, 1);
  // print the number of seconds since reset:
  lcd.print(distancia);
  delay(10);
  Serial.print(duration);
  Serial.print('\t');
  Serial.println(distancia);
}

// code stored in the sketch: ciencia_9.ino
#include <LiquidCrystal.h>

LiquidCrystal lcd(12, 11, 5, 4, 3, 2);

byte smiley[8] = {
  B00000,
  B10001,
  B00000,
  B00000,
  B10001,
  B01110,
  B00000,
};

void setup() {
  lcd.createChar(0, smiley);
  lcd.begin(16, 2);  
  lcd.write(byte(0));
}

void loop() {}
