# Fritzing sketch leds (saved by Fritzing 0.9.3b)
breadboards: 1

parts:
  LED1 = RGB LED (com. cathode, rgb) [package="5 mm [THT]"]
  LED2 = RGB LED (com. cathode, rgb) [package="5 mm [THT]"]
  LED3 = LED - 5mm [color="White (4500K)" package="5 mm [THT]"]
  S1 = Pushbutton [package="[THT]"]
  S2 = Pushbutton [package="[THT]"]
  S3 = Pushbutton [package="[THT]"]
  S4 = Pushbutton [package="[THT]"]
  R1 = Resistor [tolerance=±5% resistance=1k package=THT]
  R2 = Resistor [tolerance=±5% resistance=1k package=THT]
  R3 = Resistor [tolerance=±5% resistance=1k package=THT]
  R4 = Resistor [tolerance=±5% resistance=1k package=THT]
  R5 = Resistor [tolerance=±5% resistance=1k package=THT]
  R6 = Rotary Potentiometer (Large) [maximum_resistance=10kΩ package=THT]

nets:
  N1: LED1.common_cathode, LED3.cathode, R2.Pin_1
  N2: LED2.red_anode, S3.Pin_1, S3.Pin_2
  N3: LED2.green_anode, S4.Pin_1, S4.Pin_2
  N4: LED2.blue_anode, S2.Pin_3, S2.Pin_4
  N5: LED3.anode, S1.Pin_1, S1.Pin_2
  N6: S1.Pin_3, S1.Pin_4
  N7: S2.Pin_1, S2.Pin_2, R4.Pin_1
  N8: S3.Pin_3, S3.Pin_4, R1.Pin_0
  N9: S4.Pin_3, S4.Pin_4, R3.Pin_1
  N10: R1.Pin_1, R4.Pin_0
  N11: R2.Pin_0, R3.Pin_0
  N12: R5.Pin_0, R6.wiper
