# Fritzing sketch liga_led_arduino (saved by Fritzing 0.9.3b)
breadboards: 1

parts:
  R1 = Resistor [tolerance=±5% resistance=680 package=THT]
  Componente1 = Arduino Uno (Rev3)
  S1 = Pushbutton [package="[THT]"]
  LED1 = LED - 5mm [color="Red (633nm)" package="5 mm [THT]"]
  R2 = Resistor [tolerance=±5% resistance=330k package=THT]

nets:
  N1: R1.Pin_0, Componente1.D3_PWM
  N2: R1.Pin_1, LED1.cathode
  N3: Componente1.D4, S1.Pin_3, S1.Pin_4, R2.Pin_1
  N4: Componente1.5V, R2.Pin_0
  N5: Componente1.GND, S1.Pin_1, S1.Pin_2, LED1.anode

// code stored in the sketch: liga_led_arduino.ino

const int buttonPin = 4;
const int ledPin       = 3;
int ledValue;

void setup(){
	pinMode(ledPin,OUTPUT);
	pinMode(buttonPin,INPUT);
}

void loop(){
	ledValue = digitalRead(buttonPin);
	digitalWrite(ledPin,ledValue);
}
