# Fritzing sketch sensor capacitivo e LDR (saved by Fritzing 0.9.3b)
breadboards: 1

parts:
  R1 = Photocell (LDR) [package=THT]
  R2 = Resistor [tolerance=±5% resistance=220 package=THT]
  R3 = Resistor [tolerance=±5% resistance=220 package=THT]
  LED1 = LED - 5mm [color="Red (633nm)" package="5 mm [THT]"]
  Componente1 = Arduino Uno (Rev3)
  LED2 = LED - 5mm [color="Green (555nm)" package="5 mm [THT]"]
  R4 = Resistor [tolerance=±5% resistance=220 package=THT]
  R5 = Resistor [tolerance=±5% resistance=1M package=THT]
  J1 = Piezo Speaker

nets:
  N1: R1.pin_1, R3.Pin_0, Componente1.GND, R4.Pin_0, J1.pin1
  N2: R2.Pin_1, Componente1.A0
  N3: R3.Pin_1, LED1.cathode
  N4: LED1.anode, Componente1.D3_PWM
  N5: Componente1.D8, R5.Pin_1
  N6: Componente1.D10_PWM/SS, R5.Pin_0
  N7: Componente1.D12/MISO, J1.pin2
  N8: Componente1.D4, LED2.anode
  N9: LED2.cathode, R4.Pin_1
