# Fritzing sketch simples (saved by Fritzing 0.9.3b)
breadboards: 1

parts:
  R1 = Resistor [tolerance=±5% resistance=220 package=THT]
  LED2 = RGB LED (com. cathode, rbg) [package="5 mm [THT]"]
  R2 = Resistor [tolerance=±5% resistance=220 package=THT]
  R3 = Resistor [tolerance=±5% resistance=220 package=THT]
  R4 = Resistor [tolerance=±5% resistance=220 package=THT]
  part = RGB LED (com. cathode, rbg) [package="5 mm [THT]"]  # not connected
  LED1 = LED - 5mm [color="Red (633nm)" package="5 mm [THT]"]
  R5 = Rotary Potentiometer (Small) [maximum_resistance=100kΩ package=THT]
  Arduino1 = Arduino Uno (Rev3)

nets:
  N1: R1.Pin_0, LED1.anode
  N2: LED2.red_anode, R2.Pin_1
  N3: LED2.common_cathode, Arduino1.GND
  N4: LED2.blue_anode, R4.Pin_1
  N5: LED2.green_anode, R3.Pin_1
  N6: LED1.cathode, R5.leg1
  N7: R5.wiper, Arduino1.A0
