# Fritzing sketch sonar (saved by Fritzing 0.9.3b)
breadboards: 1

parts:
  J1 = Basic Servo
  Arduino3 = Arduino Uno (Rev3)
  hc-sr1 = hc-sr04

nets:
  GND: J1.gnd, Arduino3.GND, hc-sr1.GND
  VCC: J1.vcc, Arduino3.5V, hc-sr1.VCC
  N1: J1.pulse, Arduino3.D12/MISO
  N2: Arduino3.D10_PWM/SS, hc-sr1.Trig
  N3: Arduino3.D11_PWM/MOSI, hc-sr1.Echo
