# Fritzing sketch varia_rgb_arduino (saved by Fritzing 0.9.3b)
breadboards: 1

parts:
  R1 = Resistor [tolerance=±5% resistance=680 package=THT]
  Componente1 = Arduino Uno (Rev3)
  S1 = Pushbutton [package="[THT]"]
  R2 = Resistor [tolerance=±5% resistance=330k package=THT]
  LED1 = RGB LED - (4 legs) [package="5 mm [THT]"]
  R4 = Resistor [tolerance=±5% resistance=680 package=THT]
  R5 = Resistor [tolerance=±5% resistance=680 package=THT]
  R3 = Rotary Potentiometer (Large) [maximum_resistance=100kΩ package=THT]

nets:
  N1: R1.Pin_0, Componente1.D3_PWM
  N2: R1.Pin_1, LED1.red_cathode
  N3: Componente1.A4/SDA, R3.wiper
  N4: Componente1.D4, S1.Pin_3, S1.Pin_4, R2.Pin_1
  N5: Componente1.D5_PWM, R4.Pin_1
  N6: Componente1.D6_PWM, R5.Pin_1
  N7: Componente1.5V, R2.Pin_0, LED1.common_anode, R3.leg1
  N8: Componente1.GND, S1.Pin_1, S1.Pin_2, R3.leg2
  N9: LED1.green_cathode, R4.Pin_0
  N10: LED1.blue_cathode, R5.Pin_0

// code stored in the sketch: ciencia_3.ino
const int buttonPin = 4;
const int r   = 3;
const int g   = 5;
const int b   = 6;
int ledValue;
int lastValue;

int color = r;

void setup(){
  pinMode(r,OUTPUT);
  pinMode(g,OUTPUT);
  pinMode(b,OUTPUT);
  pinMode(buttonPin,INPUT);
}

void loop(){
  ledValue = digitalRead(buttonPin);
  if(lastValue == LOW && ledValue == HIGH){
    digitalWrite(color,HIGH);  
  } else if(lastValue == HIGH && ledValue == LOW){
    digitalWrite(color,LOW);
    int newColor;
    if (color == r){
      newColor = g;
    }
    if (color == g){
      newColor = b;
    }
    if (color == b){
      newColor = r;
    }
    color = newColor;
  }
  lastValue = ledValue;
}

// code stored in the sketch: ciencia_4.ino
const int buttonPin = 4;
const int r   = 3;
const int g   = 5;
const int b   = 6;

const int potPin = A4;

int ledValue;
int buttonValue;
int lastValue;

int color = r;

void setup(){
  pinMode(r,OUTPUT);
  pinMode(g,OUTPUT);
  pinMode(b,OUTPUT);
  pinMode(buttonPin,INPUT);
}

void loop(){
  buttonValue = digitalRead(buttonPin);
  if(lastValue == HIGH && buttonValue == LOW){
    digitalWrite(color,LOW);
    int newColor;
    if (color == r){
      newColor = g;
    }
    if (color == g){
      newColor = b;
    }
    if (color == b){
      newColor = r;
    }
    color = newColor;
    ledValue = 0;
  }
  if (buttonValue == HIGH){
    ledValue = analogRead(potPin)/4;
  }
  lastValue = buttonValue;
  analogWrite(color,ledValue);
  delay(10);
}

// code stored in the sketch: liga_led_arduino.ino

const int buttonPin = 4;
const int ledPin       = 3;
int ledValue;

void setup(){
	pinMode(ledPin,OUTPUT);
	pinMode(buttonPin,INPUT);
}

void loop(){
	ledValue = digitalRead(buttonPin);
	digitalWrite(ledPin,ledValue);
}

// code stored in the sketch: setHue.ino
const int potPin = A0; // Precisa ser analógico
const int rPin   = 3; // precisa ser PWM
const int gPin   = 5; // precisa ser PWM
const int bPin   = 6; // precisa ser PWM

void setup(){
  pinMode(potPin,INPUT);
  pinMode(rPin,OUTPUT);
  pinMode(rPin,OUTPUT);
  pinMode(rPin,OUTPUT);
}

void loop(){
  setHue(analogRead(potPin, rPin, gpIn, bPin));
}

// A função setHue define os valores analógicos (PWM)
// dos pinos r, g e b em função da definição de hue
void setHue(int hue, int r, int g, int b){
  // Função a ser definida
}
